// Digital circuit Assignment2LabibAlashwalCIS310.dig as structural Verilog
module Assignment2LabibAlashwalCIS310 (
  input  [1:0] WriteRegister,
  input  [1:0] ReadRegister1,
  input  [1:0] ReadRegister2,
  input  [1:0] ALUControl,
  output [7:0] ReadData1,
  output [7:0] ReadData2,
  output [7:0] ALUResult
);

  wire decoder_1_out_0, decoder_1_out_1, decoder_1_out_2, decoder_1_out_3;
  wire [7:0] add_1_s, and_1_out, multiplexer_1_out, or_1_out, R0_q, R1_q, R2_q, R3_q, sub_1_s;

  Decoder #(.Selector_Bits(2)) decoder_1 (
    .out_0(decoder_1_out_0), .out_1(decoder_1_out_1), .out_2(decoder_1_out_2), .out_3(decoder_1_out_3));  // open: sel
  Register #(.Bits(8)) R0 (.C(decoder_1_out_0), .Q(R0_q));  // open: D, en
  Register #(.Bits(8)) R1 (.C(decoder_1_out_1), .Q(R1_q));  // open: D, en
  Register #(.Bits(8)) R2 (.C(decoder_1_out_2), .Q(R2_q));  // open: D, en
  Register #(.Bits(8)) R3 (.C(decoder_1_out_3), .Q(R3_q));  // open: D, en
  Multiplexer #(.Selector_Bits(2), .Bits(8)) multiplexer_1 (
    .sel(ReadRegister2), .out(multiplexer_1_out));  // open: in_0, in_1, in_2, in_3
  Multiplexer #(.Bits(8), .Selector_Bits(2)) multiplexer_2 (
    .sel(ReadRegister1), .in_0(R0_q), .in_1(R1_q), .in_2(R2_q), .in_3(R3_q), .out(ReadData1));
  Add add_1 (.a(ReadData1[0]), .b(multiplexer_1_out[0]), .s(add_1_s[0]));  // open: c_i, c_o
  Sub sub_1 (.a(ReadData1[0]), .b(multiplexer_1_out[0]), .s(sub_1_s[0]));  // open: c_i, c_o
  and and_1 (and_1_out[0], ReadData1[0], multiplexer_1_out[0]);
  or or_1 (or_1_out[0], ReadData1[0], multiplexer_1_out[0]);
  Multiplexer #(.Bits(8), .Selector_Bits(2)) multiplexer_3 (
    .sel(ALUControl), .in_0(add_1_s), .in_1(sub_1_s), .in_2(and_1_out), .in_3(or_1_out), .out(ALUResult));
  // Pins of 1 and 8 bits meet at ReadData1
  // Pins of 1 and 8 bits meet at multiplexer_1_out
  // Pins of 1 and 8 bits meet at add_1_s
  // Pins of 1 and 8 bits meet at sub_1_s
  // Pins of 1 and 8 bits meet at and_1_out
  // Pins of 1 and 8 bits meet at or_1_out
endmodule
